# Fritzing sketch DigitalSWITCH_TOGGLE_TWO-LED (saved by Fritzing 0.9.3b)
breadboards: 1

parts:
  Part1 = Adafruit Feather M0 Basic Proto [part_number="Adafruit #2772"]
  R1 = Resistor [tolerance=±5% resistance=220 package="2010 [SMD]"]
  S1 = Pushbutton [package="[SMD]"]
  R2 = Resistor [tolerance=±5% resistance=10k package="0805 [SMD]"]
  LED1 = smd LED [color="Red (633nm)" package="1206 [SMD]"]
  LED2 = smd LED [color="Red (633nm)" package="1206 [SMD]"]
  R3 = Resistor [tolerance=±5% resistance=220 package="2010 [SMD]"]

nets:
  N1: Part1.A5, S1.Pin_3, S1.Pin_4, R2.Pin_1
  N2: Part1.A1, LED2.anode
  N3: Part1.A0, LED1.anode
  N4: Part1.GND, R1.Pin_1, R2.Pin_0, R3.Pin_1
  N5: Part1.+3V3, S1.Pin_1, S1.Pin_2
  N6: R1.Pin_0, LED1.cathode
  N7: LED2.cathode, R3.Pin_0

custom parts:
  Adafruit Feather M0 Basic Proto: At the Feather M0's heart is an ATSAMD21G18 ARM Cortex M0 processor, clocked at 48 MHz and at 3.3V logic, the same one used in the new Arduino Zero. This chip has a whopping 256K of FLASH (8x more than the Atmega328 or 32u4) and 32K of RAM (16x as much)! This chip comes with built in USB so it has USB-to-Serial program & debug capability built in with no need for an FTDI-like chip. To make it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

// code stored in the sketch: DigitalLED.ino
/* Here we declare variables to store data in our program
 * variables use a little bit of memory to store a little bit of data of different types
 * data types (int, long, float, double, uint_16, char, string etc.) determine what kind of data is stored in memory
 * 
 * there are two types of memory: program and dynamic
 * program memory stores all of the compiled code you write and other things you want to place there
 * it says static until the uC is reprogrammed (from the upload button in this case)
 * dynamic memory stores information for the short term and it can change over the course of a program
 * variables have a SCOPE which is like visibility to parts of the program
 * if a variable is declared outside of any brackets or braces its scope is GLOBAL
 * global variables consume dynamic memory for the entire run of a program 
 * global variables have a set type but their values can change (unless declared const - constant)
 * if a variable is declared inside a set of curly braces {} that varible is can only be used by code that is also in the braces
 * after the code in the braces has run the memory for that varible can be used by another part of a program
 * that memory is dynamic; it is volitile. 
 */

//these global variables give names to pin numbers
const int led1 = A0;

//these global variables control timing
int onDelay = 500;
int offDelay = 250;

// put setup code here, to run once when the uC is powered on:
void setup() {
  /* 
   *  pinMode is a function we need to call. Function calls usually look like this: function();
   *  Anything placed in the () is called an argument
   *  The pinMode() function takes two arguments: an integer and a keyword
   *  led1 is an integer global variable and OUTPUT is a keyword
   *  We could also use INPUT or INPUT_PULLUP as keywords to change how the pin functions.
   *  
   *  You will also notice that setup() above and loop() below are also functions. 
   *  However setup() and loop() have a declaration in front of them (void)
   *  Just like the variable type (int) above, void is also a type
   *  Just like we declared variables above we are declaring setup() and loop() only with a void type...
   *  Void means a function does not return a value. If a function is declared with a data type it can also return a value.
   *  We now know the structure for declaring and calling both variables and functions.
  */
  pinMode(led1, OUTPUT);
}

// put other code here, to run repeatedly:
void loop() {
  //digitalWrite() uses two arguments (int pin# and digital state (HIGH/LOW || 1/0)) to control a digital output
  digitalWrite(led1, HIGH);
  //delay uses one argument (int milliseconds) to pause the program for a short period of time
  delay(onDelay);
  digitalWrite(led1, LOW);
  //delay can be problematic when programs become more complex becuase nothing else can happen during a delay...
  delay(offDelay);
}

// code stored in the sketch: DigitalSWITCH-TOGGLE.ino

//these global variables give names to pin numbers
const int led1 = A0;
const int button1 = A5;

//these varibles control the led state
bool led1State = 0;  //bool is either true or fales (1 or 0)

void setup() {
  //open a serial connection for Debug output to serial monitor
  Serial.begin(9600);
  pinMode(led1, OUTPUT);
  pinMode(button1, INPUT); //this makes button1 (pin A5) a digital input!
  digitalWrite(led1, led1State);
}

void loop() {
  /*
   * Buttons are more useful when they TOGGLE things on or off
   * To toggle the LED we still read the button pin
   * but now we use it to toggle a varible on or off (1 or 0)
   * Then we use that varible to write the led state
   * There is a new global variable up above the setup() fuction
   * It will control the desired state for the LED
   */

  int buttonRead = digitalRead(button1);
  delay(1);
  //debug output to see the current reading in the serial monitor
  Serial.print("buttonRead = ");
  Serial.println(buttonRead);

  //if the button is pushed
  if(buttonRead == 1) {
    led1State = !led1State; //! will make led1State the opposite of itself
  }

digitalWrite(led1, led1State);

}

// code stored in the sketch: DigitalSWITCH-TOGGLE_TWO-LED.ino

//these global variables give names to pin numbers
const int led1 = A0;
const int led2 = A1;
const int button1 = A5;

//these constants will give names to the modes of the system
const int modeOff = 0;
const int modeLow = 1;
const int modeHigh = 2;
const int modeFlash = 3;

//this global variable will set the current mode
int lightMode = modeOff;

//this global variable will track time for flashing the leds
unsigned long flashTime;
unsigned long lastFlash;

//these varibles control the led state
int led1State = 0;  //bool is either true or fales (1 or 0)
int led2State = 0;

//these global variables will track what the last read of the switch was and the current state
int buttonReadPre = 0;
int buttonState;

//this global variable will mark when the button changes
unsigned long buttonTime;

void setup() {
  //open a serial connection for Debug output to serial monitor
  Serial.begin(9600);
  pinMode(led1, OUTPUT);

  //don't forget to declare the new led pin as an OUTPUT!
  pinMode(led2, OUTPUT);
  pinMode(button1, INPUT);
  digitalWrite(led1, led1State);
}

void loop() {
  /*
     Let's add a second LED and a couple of modes!

     There are eight new global variables:
     to name a new led pin, track it state, and three modes, plus two time flash the leds without delay!
     The first major change is to make a button push toggle between modes

     Then we need to do different things with the leds depending on the value of the mode
  */

  int buttonRead = digitalRead(button1);
  delay(1);

  if (buttonRead != buttonReadPre) {
    buttonTime = millis(); //millis(); returns the time since the program started...
  }

  int debounceTime = millis() - buttonTime; //current time minus start time is elapsed time...

  if (debounceTime >= 50) {
    if (buttonRead != buttonState) {
      buttonState = buttonRead;
      if (buttonState == 1) {

        //changed this to iterate through modes
        lightMode += 1; //+= is an iterator that adds the right hand operator to the left and saves it

        //we need to make sure we don't set the light mode to more than 3...
        //if it is more than 3
        if (lightMode > 3) {

          //cycle it back to 0
          lightMode = 0;
        }
      }
    }
  }

  /*
     now we need some new if statements to decide what to do depending on what the value of lightMode is
     these conditions are mutually exclusive so we can use if(){}else if(){}
  */

  //if the lightMode is modeOff (0)...
  if (lightMode == modeOff) {

    //set both leds to off
    led1State = 0;
    led2State = 0;
  }
  
  //otherwise if it is modeLow (1)...
  else if (lightMode == modeLow) {

    //set the first led on and the second off
    led1State = 1;
    led2State = 0;
  }
  
  //otherwise if it is modeHigh (2)...
  else if (lightMode == modeHigh) {
  //set both leds on
    led1State = 1;
    led2State = 1;
  }

  //otherwise if it is modeFlash
  else if (lightMode == modeFlash) {
    
    //check to see if the flash time is higher than 100ms
    if (flashTime >= 100) {

      //and toggle the mode of both leds if it is
      led1State = !led1State;
      led2State = !led2State;
      //and reset the lastFlash time
      lastFlash = millis();
    }
  }

  //no matter what happens update the flashTime
  flashTime = millis() - lastFlash;

  //write both of the ledstates
  digitalWrite(led1, led1State);
  digitalWrite(led2, led2State);

  //save the buttonRead as buttonReadPre
  buttonReadPre = buttonRead;
}
