# Fritzing sketch BasicLED (saved by Fritzing 0.9.3b)
breadboards: 1

parts:
  Part1 = Adafruit Feather M0 Basic Proto [part_number="Adafruit #2772"]
  LED1 = smd LED [color="Red (633nm)" package="1206 [SMD]"]
  R1 = Resistor [tolerance=±5% resistance=15 package="2010 [SMD]"]

nets:
  N1: Part1.GND, R1.Pin_0
  N2: Part1.+3V3, LED1.anode
  N3: LED1.cathode, R1.Pin_1

custom parts:
  Adafruit Feather M0 Basic Proto: At the Feather M0's heart is an ATSAMD21G18 ARM Cortex M0 processor, clocked at 48 MHz and at 3.3V logic, the same one used in the new Arduino Zero. This chip has a whopping 256K of FLASH (8x more than the Atmega328 or 32u4) and 32K of RAM (16x as much)! This chip comes with built in USB so it has USB-to-Serial program & debug capability built in with no need for an FTDI-like chip. To make it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
